# Fritzing sketch Шаблон электросхемы проекта (2)-Дима (saved by Fritzing 0.9.3b)
breadboards: 1

parts:
  Часть1 = Arduino Uno (Rev3)
  VCC1 = Battery
  S1 = Toggle Switch [package=THT]
  Часть2 = LED Matrix - Serial Interface - Red/Green/Blue
  SP1 = SPEAKER [package=pcb_mount_speaker]
  Q1 = NPN-Transistor [package="TO92 [THT]"]
  S2 = Pushbutton [package="[THT]"]
  S3 = Pushbutton [package="[THT]"]
  S4 = Pushbutton [package="[THT]"]
  S5 = Pushbutton [package="[THT]"]
  S6 = Pushbutton [package="[THT]"]
  S7 = Pushbutton [package="[THT]"]
  S8 = Pushbutton [package="[THT]"]

nets:
  N1: Часть1.D8, S2.Pin_3, S2.Pin_4
  N2: Часть1.D9_PWM, S7.Pin_3, S7.Pin_4
  N3: Часть1.D10_PWM/SS, S5.Pin_3, S5.Pin_4
  GND: Часть1.GND, S1.L2, Часть2.GND, SP1.+, S2.Pin_1, S2.Pin_2, S3.Pin_1, S3.Pin_2, S4.Pin_1, S4.Pin_2, S5.Pin_1, S5.Pin_2, S6.Pin_1, S6.Pin_2, S7.Pin_1, S7.Pin_2, S8.Pin_1, S8.Pin_2
  N4: Часть1.D2, Часть2.MOSI
  N5: Часть1.D3_PWM, Q1.B
  N6: Часть1.D4, S3.Pin_3, S3.Pin_4
  N7: Часть1.D5_PWM, S4.Pin_3, S4.Pin_4
  N8: Часть1.D6_PWM, S8.Pin_3, S8.Pin_4
  N9: Часть1.D7, S6.Pin_3, S6.Pin_4
  N10: Часть1.VIN, VCC1.+, Часть2.CS, Q1.C
  N11: VCC1.-, S1.L1
