# Fritzing sketch Шаблон электросхемы проекта (3-Дима (saved by Fritzing 0.9.3b)
breadboards: 2

parts:
  Часть2 = LED Matrix - Serial Interface - Red/Green/Blue
  SP1 = SPEAKER [package=pcb_mount_speaker]
  Q1 = NPN-Transistor [package="TO92 [THT]"]
  S2 = Pushbutton [package="[THT]"]
  S3 = Pushbutton [package="[THT]"]
  S4 = Pushbutton [package="[THT]"]
  S5 = Pushbutton [package="[THT]"]
  S6 = Pushbutton [package="[THT]"]
  S7 = Pushbutton [package="[THT]"]
  S8 = Pushbutton [package="[THT]"]
  Часть3 = Arduino Nano (Rev3.0)
  YwRobot_Power_Supply1 = YwRobot Breadboard Power Supply [part_number=545043]  # not connected

nets:
  GND: Часть2.GND, Часть2.CS, SP1.+, Q1.B, Q1.C, S2.Pin_1, S2.Pin_2, S3.Pin_1, S3.Pin_2, S4.Pin_1, S4.Pin_2, S5.Pin_1, S5.Pin_2, S6.Pin_1, S6.Pin_2, S7.Pin_1, S7.Pin_2, S8.Pin_1, S8.Pin_2, S8.Pin_3, S8.Pin_4, Часть3.GND, Часть3.D8, Часть3.VIN
  N1: Часть2.MOSI, Часть3.RESET
  N2: S2.Pin_3, S2.Pin_4, Часть3.D3
  N3: S3.Pin_3, S3.Pin_4, Часть3.D6
  N4: S4.Pin_3, S4.Pin_4, Часть3.D7
  N5: S5.Pin_3, S5.Pin_4, Часть3.D5
  N6: S6.Pin_3, S6.Pin_4, Часть3.D2
  N7: S7.Pin_3, S7.Pin_4, Часть3.D4

custom parts:
  YwRobot Breadboard Power Supply: The YwRobot Breadboard Power Supply (MB-V2) has two power rails; they can be 5V or 3V3. Power to the module can be provided through the female USB socket or through the A10 (female) 2.1mm power jack.
